// Logisim project decoder 3 by 8.circ as structural Verilog: 1 circuit, main circuit main
module main (
  input  A,
  input  B,
  input  C,
  output D0,
  output D1,
  output D2,
  output D3,
  output D4,
  output D5,
  output D6,
  output D7
);

  wire and_1_out, and_2_out, and_3_out, and_4_out, and_5_out, and_6_out, not_1_out, not_2_out, not_3_out;

  not not_1 (not_1_out, A);
  not not_2 (not_2_out, B);
  not not_3 (not_3_out, C);
  and and_1 (and_1_out, not_1_out, not_2_out);
  and and_2 (and_2_out, not_1_out, B);
  and and_3 (and_3_out, not_1_out, B);
  and and_4 (and_4_out, A, not_2_out);
  and and_5 (and_5_out, A, not_2_out);
  and and_6 (and_6_out, A, B);
  and and_7 (D0, and_1_out, not_3_out);
  and and_8 (D1, and_1_out, C);
  and and_9 (D2, and_2_out, not_3_out);
  and and_10 (D3, and_3_out, C);
  and and_11 (D4, and_4_out, not_3_out);
  and and_12 (D5, and_5_out, C);
  and and_13 (D6, and_6_out, not_3_out);
  and and_14 (D7, and_6_out, C);
endmodule
