// Logisim project encoder & decoder.circ as structural Verilog: 1 circuit, main circuit main
module main (
  input  D3,
  input  Q0,
  input  D2,
  input  Q1,
  input  D1,
  output Q1_2,
  output D0,
  output D1_2,
  output Q0_2,
  output D2_2,
  output D3_2
);

  wire not_1_out, not_2_out;

  not not_1 (not_1_out, Q0);
  not not_2 (not_2_out, Q1);
  and and_1 (D0, not_1_out, not_2_out);
  and and_2 (D1_2, not_2_out, Q0);
  and and_3 (D2_2, not_1_out, Q1);
  and and_4 (D3_2, Q1, Q0);
  or or_1 (Q1_2, D3, D2);
  or or_2 (Q0_2, D3, D1);
endmodule
