// Logisim project encoder 8 by 3.circ as structural Verilog: 1 circuit, main circuit main
module main (
  input  D0,
  input  D1,
  input  D2,
  input  D3,
  input  D4,
  input  D5,
  input  D6,
  input  D7,
  output C,
  output B,
  output A
);

  wire and_1_out, and_2_out, and_3_out, and_4_out, and_5_out, and_6_out, and_7_out, not_1_out, not_2_out,
       not_3_out, not_4_out, not_5_out, not_6_out, or_1_out, or_2_out, or_3_out, or_5_out, or_6_out;

  not not_1 (not_1_out, D2);
  not not_2 (not_2_out, D4);
  not not_3 (not_3_out, D3);
  or or_1 (or_1_out, D2, D3);
  or or_2 (or_2_out, D4, D5);
  or or_3 (or_3_out, D6, D7);
  not not_4 (not_4_out, D6);
  and and_1 (and_1_out, D1, not_1_out);
  and and_2 (and_2_out, not_2_out, not_3_out);
  not not_5 (not_5_out, D4);
  not not_6 (not_6_out, D5);
  and and_3 (and_3_out, and_1_out, and_2_out);
  and and_4 (and_4_out, not_5_out, not_6_out);
  or or_4 (A, or_2_out, or_3_out);
  and and_5 (and_5_out, D3, not_2_out);
  or or_5 (or_5_out, and_5_out, and_3_out);
  and and_6 (and_6_out, or_1_out, and_4_out);
  or or_6 (or_6_out, or_5_out, D5);
  or or_7 (B, and_6_out, or_3_out);
  and and_7 (and_7_out, or_6_out, not_4_out);
  or or_8 (C, and_7_out, D7);
endmodule
